# Fritzing sketch ardrando (saved by Fritzing 0.9.4)
breadboards: 1

parts:
  S1 = Toggle Switch [package=THT]
  LED1 = LED - 3mm [color="Red (633nm)" package="3 mm [THT]"]
  LED2 = LED - 3mm [color="Blue (470nm)" package="3 mm [THT]"]
  LED3 = LED - 3mm [color="Green (565nm)" package="3 mm [THT]"]
  Part2 = adafruit [part_number=DAC]
  R4 = Resistor [tolerance=±5% resistance=220 package="0805 [SMD]"]
  R5 = Resistor [tolerance=±5% resistance=220 package="0805 [SMD]"]
  R6 = Resistor [tolerance=±1% resistance=220 package="0805 [SMD]"]
  R7 = Resistor [tolerance=±1% resistance=8.2 package=THT]
  R8 = Resistor [tolerance=±1% resistance=5.6k package=THT]
  Power_Header = Header 5x2 [package=2x5-shrouded_smd]
  CLOCK_IN = AUDIO-JACK2 [package=audio-jack-3.5mm-smd]
  GATE_OUT = AUDIO-JACK2 [package=audio-jack-3.5mm-smd]
  Volt/Octave_OUT = AUDIO-JACK2 [package=audio-jack-3.5mm-smd]
  Part1 = Arduino Nano (Rev3.0)
  U7 = POT [package=alps_pot]
  U10 = POT [package=alps_pot]
  U11 = POT [package=alps_pot]

nets (from the schematic view):
  GND: S1.L1, S1.COM, Part2.connector10, Part2.connector13, R4.Pin_1, R5.Pin_1, R6.Pin_1, Power_Header.3, Power_Header.4, Power_Header.5, Power_Header.6, Power_Header.7, Power_Header.8, GATE_OUT.SLEEVE, Volt/Octave_OUT.SLEEVE, U7.A, U10.A, U11.A
  N1: S1.L2, Part1.D6
  N2: LED1.cathode, R6.Pin_0
  N3: LED1.anode, Part1.D2
  N4: LED2.cathode, R5.Pin_0
  N5: LED2.anode, Part1.D3
  N6: LED3.cathode, R4.Pin_0
  N7: LED3.anode, Part1.D4
  5V: Part2.connector9, Part1.5V, U7.E, U10.E, U11.E
  SCL: Part2.connector11, Part1.A5
  SDA: Part2.connector12, Part1.A4
  N8: Part2.connector14, Volt/Octave_OUT.TIP
  TRIG_IN: R7.Pin_0, R8.Pin_0, Part1.A1
  N9: R7.Pin_1, CLOCK_IN.TIP
  N10: R8.Pin_1, CLOCK_IN.SLEEVE
  N11: Power_Header.1, Power_Header.2
  12V: Power_Header.9, Power_Header.10, Part1.VIN
  GATE_OUT: GATE_OUT.TIP, Part1.D5
  length: Part1.A7, U7.S
  scale: Part1.A6, U11.S
  random: Part1.A3, U10.S

notes:
  ArdRando, Simple quantized random sequence generator, 1
